// Logisim project Perfectos.circ as structural Verilog
module BOARD_BIG_ASM (
  output out_1
);

  wire button_1_out, CLK, CLR, d_ff_1_q, not_1_out, Write, Write_ASCII;
  wire [6:0] ASCII;
  wire [7:0] counter_1_q;
  wire [23:0] Dir_INPUT, Dir_MEMORY;
  wire [31:0] INPUT, MEMORY_IN, MEMORY_OUT;

  Button button_1 (.out(button_1_out));
  Clock clock_1 (.out(CLK));
  D_Flip_Flop d_ff_1 (.clk(CLK), .D(1'b1), .Q(d_ff_1_q), .reset(button_1_out));  // open: Qn, preset, en
  D_Flip_Flop d_ff_2 (.clk(CLK), .D(d_ff_1_q), .Qn(CLR), .reset(button_1_out));  // open: Q, preset, en
  BIG_ASM big_asm_1 (
    .DATA_INPUT(INPUT), .MEMORY_IN(MEMORY_OUT), .CLK(CLK), .CLR(CLR), .DIR_INPUT(Dir_INPUT),
    .MEMORY_OUT(MEMORY_IN), .DIR_MEMORY(Dir_MEMORY), .Write_OUTPUT(Write), .ASCII(ASCII),
    .Write_ASCII(Write_ASCII), .END(out_1));
  MEMORY memory_1 (.DIR(Dir_MEMORY), .DATA_IN(MEMORY_IN), .WRITE(Write), .CLK(CLK), .CLR(CLR), .DATA_OUT(MEMORY_OUT));
  INPUT input_1 (.DIR(Dir_INPUT), .CLK(CLK), .DATA_OUT(INPUT));
  Counter counter_1 (.load(1'b0), .count(not_1_out), .Q(counter_1_q), .clk(CLK), .clr(CLR));  // open: D, carry
  not not_1 (not_1_out, out_1);
  // Probe on counter_1_q
  TTY #(.rows(32), .cols(60)) tty_1 (.data(ASCII), .clk(CLK), .we(Write_ASCII), .clr(CLR));

  // Other names for the same wires on the sheet: END = out_1

  // Notes on the sheet:
  //   COUNTER
  //   BOARD
endmodule

module INPUT (
  input  [23:0] DIR,
  input  CLK,
  output [31:0] DATA_OUT
);

  RAM #(.addrWidth(24), .dataWidth(32)) ram_1 (.addr(DIR), .data(DATA_OUT), .clk(CLK), .ld(1'b1));  // open: sel, clr
endmodule

module MEMORY (
  input  [23:0] DIR,
  input  [31:0] DATA_IN,
  input  WRITE,
  input  CLK,
  input  CLR,
  output [31:0] DATA_OUT
);

  wire not_1_out;

  not not_1 (not_1_out, WRITE);
  RAM #(.addrWidth(24), .dataWidth(32), .bus("separate")) ram_1 (
    .addr(DIR), .din(DATA_IN), .data(DATA_OUT), .str(WRITE), .clk(CLK), .ld(not_1_out), .clr(CLR));  // open: sel
endmodule

module BIG_ASM (
  input  [31:0] DATA_INPUT,
  input  [31:0] MEMORY_IN,
  input  CLK,
  input  CLR,
  output [23:0] DIR_INPUT,
  output [31:0] MEMORY_OUT,
  output [23:0] DIR_MEMORY,
  output Write_OUTPUT,
  output [6:0] ASCII,
  output Write_ASCII,
  output END
);

  wire printmany_starter_1_start, start;
  wire [23:0] m, m1;

  starter starter_1 (.in_1(CLR), .in_2(CLK), .start(start));
  PrintMany___starter printmany_starter_1 (.in_1(END), .in_2(CLK), .start(printmany_starter_1_start), .in_3(CLR));
  Perfectos_n___ASM perfectos_n_asm_1 (
    .in_1(start), .in_2(CLR), .in_4(DATA_INPUT), .out_7(m), .out_8(MEMORY_OUT), .out_6(END),
    .out_5(Write_OUTPUT), .in_3(CLK));
  PrintMany printmany_1 (
    .in_3(printmany_starter_1_start), .in_4(CLR), .in_5(CLK), .out_7(m1), .out_9(ASCII), .in_1(MEMORY_IN),
    .in_2(m), .out_8(Write_ASCII));  // open: out_6
  Multiplexer #(.width(24), .disabled(0), .enable("false")) multiplexer_1 (
    .in0(m), .in1(m1), .out(DIR_MEMORY), .sel(END));

  assign DIR_INPUT = {24{1'b0}};

  // Other names for the same wires on the sheet: D_Out[31:0] = MEMORY_OUT; M_I[31:0] = MEMORY_IN;
  //   n[31:0] = DATA_INPUT; rst = CLR; w = Write_OUTPUT
endmodule

module PRINT_UDEC (
  input  [31:0] num,
  input  start,
  input  CLK,
  input  RST,
  output [6:0] ASCII,
  output Write_ASCII,
  output \end 
);

  wire _0_c, _0_n, demultiplexer_1_out0, demultiplexer_2_out0, demultiplexer_2_out1, demultiplexer_3_out0,
       demultiplexer_3_out1, IDLE_2_q, IDLE_3_q, IDLE_4_q, IDLE_q, Lc, Lc_0, Ln, Ln_0, or_1_out;
  wire [23:0] bit_extender_1_out;
  wire [31:0] c, c___1, c___1_t, divider_1_rem, memory_1_data_out, multiplexer_1_out, multiplexer_2_out,
       multiplexer_3_out, n, n___10, n___10___48;

  Multiplexer #(.width(32), .enable("false")) multiplexer_1 (
    .in0(num), .in1(n___10), .out(multiplexer_1_out), .sel(Lc_0));
  Divider #(.width(32)) divider_1 (.a(n), .b(32'ha), .out(n___10), .rem(divider_1_rem));  // open: upper
  Adder #(.width(32)) adder_1 (.a(divider_1_rem), .b(32'h30), .out(n___10___48));  // open: cin, cout
  or or_1 (or_1_out, demultiplexer_1_out0, \end );
  Register #(.width(32)) u_n (.D(multiplexer_1_out), .en(Ln), .Q(n), .clk(CLK), .clr(RST));
  D_Flip_Flop IDLE (.clk(CLK), .D(or_1_out), .Q(IDLE_q), .preset(RST));  // open: Qn, en, reset
  Demultiplexer #(.enable("false")) demultiplexer_1 (
    .out0(demultiplexer_1_out0), .out1(Ln_0), .in(IDLE_q), .sel(start));
  or or_2 (Write_ASCII, demultiplexer_3_out0, demultiplexer_2_out1);
  Multiplexer #(.width(32), .enable("false")) multiplexer_2 (
    .in0(c___1), .in1(c___1_t), .out(multiplexer_2_out), .sel(Write_ASCII));
  Adder #(.width(32)) adder_2 (.a(c), .b(32'h1), .out(c___1));  // open: cin, cout
  Subtractor #(.width(32)) subtractor_1 (.a(c), .b(32'h1), .out(c___1_t));  // open: bin, bout
  D_Flip_Flop IDLE_2 (.clk(CLK), .D(Ln_0), .Q(IDLE_2_q), .reset(RST));  // open: Qn, preset, en
  Register #(.width(32)) u_c (.D(multiplexer_2_out), .en(Lc), .Q(c), .clk(CLK), .clr(RST));
  or or_3 (Lc_0, IDLE_2_q, demultiplexer_3_out1);
  Multiplexer #(.width(32), .enable("false")) multiplexer_3 (
    .in0(c), .in1(c___1_t), .out(multiplexer_3_out), .sel(Write_ASCII));
  Comparator #(.width(32), .mode("unsigned")) comparator_1 (.a({32{1'b0}}), .b(n), .lt(_0_n));  // open: gt, eq
  Comparator #(.width(32), .mode("unsigned")) comparator_2 (.a({32{1'b0}}), .b(c), .lt(_0_c));  // open: gt, eq
  D_Flip_Flop IDLE_3 (.clk(CLK), .D(Write_ASCII), .Q(IDLE_3_q), .reset(RST));  // open: Qn, preset, en
  Demultiplexer #(.enable("false")) demultiplexer_2 (
    .out0(demultiplexer_2_out0), .out1(demultiplexer_2_out1), .in(IDLE_3_q), .sel(_0_c));
  Bit_Extender #(.in_width(32), .out_width(24)) bit_extender_1 (.in(multiplexer_3_out), .out(bit_extender_1_out));
  D_Flip_Flop IDLE_4 (.clk(CLK), .D(Lc_0), .Q(IDLE_4_q), .reset(RST));  // open: Qn, preset, en
  or or_4 (Lc, Lc_0, Write_ASCII);
  or or_5 (Ln, Ln_0, Lc_0);
  Demultiplexer #(.enable("false")) demultiplexer_3 (
    .out0(demultiplexer_3_out0), .out1(demultiplexer_3_out1), .in(IDLE_4_q), .sel(_0_n));
  D_Flip_Flop IDLE_5 (.clk(CLK), .D(demultiplexer_2_out0), .Q(\end ), .reset(RST));  // open: Qn, preset, en
  MEMORY memory_1 (
    .DIR(bit_extender_1_out), .DATA_IN(n___10___48), .WRITE(Lc_0), .CLK(CLK), .CLR(RST),
    .DATA_OUT(memory_1_data_out));
  Bit_Extender #(.in_width(32), .out_width(7)) bit_extender_2 (.in(memory_1_data_out), .out(ASCII));

  // Other names for the same wires on the sheet: Lc_1 = Write_ASCII; Sc = Write_ASCII; Ln_1 = Lc_0; Sn = Lc_0;
  //   Write = Lc_0
endmodule

module PRINT_DEC (
  input  [31:0] num,
  input  start,
  input  CLK,
  input  RST,
  output [6:0] ASCII,
  output Write_ASCII,
  output END
);

  wire demultiplexer_1_out0, demultiplexer_1_out1, demultiplexer_2_out0, demultiplexer_3_out0, end_t,
       IDLE_3_q, IDLE_q, or_1_out, or_2_out, or_3_out, S_ASCII, startUDEC, Write_ASCII_1;
  wire [6:0] ASCII_t;
  wire [31:0] multiplexer_1_out, negator_1_out;

  or or_1 (or_1_out, demultiplexer_1_out0, END);
  Negator #(.width(32)) negator_1 (.in(num), .out(negator_1_out));
  D_Flip_Flop IDLE (.clk(CLK), .D(or_1_out), .Q(IDLE_q), .preset(RST));  // open: Qn, en, reset
  Demultiplexer #(.enable("false")) demultiplexer_1 (
    .out0(demultiplexer_1_out0), .out1(demultiplexer_1_out1), .in(IDLE_q), .sel(start));
  Multiplexer #(.width(32), .enable("false")) multiplexer_1 (
    .in0(num), .in1(negator_1_out), .out(multiplexer_1_out), .sel(num[31]));
  Demultiplexer #(.enable("false")) demultiplexer_2 (
    .out0(demultiplexer_2_out0), .out1(S_ASCII), .in(demultiplexer_1_out1), .sel(num[31]));
  or or_2 (or_2_out, demultiplexer_2_out0, S_ASCII);
  D_Flip_Flop IDLE_2 (.clk(CLK), .D(or_2_out), .Q(startUDEC), .reset(RST));  // open: Qn, preset, en
  PRINT_UDEC print_udec_1 (
    .num(multiplexer_1_out), .start(startUDEC), .CLK(CLK), .RST(RST), .ASCII(ASCII_t),
    .Write_ASCII(Write_ASCII_1), .\end (end_t));
  D_Flip_Flop IDLE_3 (.clk(CLK), .D(or_3_out), .Q(IDLE_3_q), .reset(RST));  // open: Qn, preset, en
  or or_3 (or_3_out, startUDEC, demultiplexer_3_out0);
  Demultiplexer #(.enable("false")) demultiplexer_3 (
    .out0(demultiplexer_3_out0), .out1(END), .in(IDLE_3_q), .sel(end_t));
  Multiplexer #(.width(7), .enable("false")) multiplexer_2 (
    .in0(ASCII_t), .in1(7'b0101101), .out(ASCII), .sel(S_ASCII));
  or or_4 (Write_ASCII, S_ASCII, Write_ASCII_1);

  // Other names for the same wires on the sheet: sign = num[31]; Write_ASCII_0 = S_ASCII
endmodule

module TEST_PRINT (
  input  [31:0] in_1,
  output out_2
);

  wire button_1_out, button_2_out, CLK, CLR, d_ff_1_q, Write_ASCII;
  wire [6:0] ASCII;

  Button button_1 (.out(button_1_out));
  Clock clock_1 (.out(CLK));
  D_Flip_Flop d_ff_1 (.clk(CLK), .D(1'b1), .Q(d_ff_1_q), .reset(button_1_out));  // open: Qn, preset, en
  D_Flip_Flop d_ff_2 (.clk(CLK), .D(d_ff_1_q), .Qn(CLR), .reset(button_1_out));  // open: Q, preset, en
  Button button_2 (.out(button_2_out));
  PRINT_UDEC print_udec_1 ();  // open: num, start, CLK, RST, ASCII, Write_ASCII, end
  PRINT_DEC print_dec_1 (
    .num(in_1), .start(button_2_out), .CLK(CLK), .RST(CLR), .ASCII(ASCII), .Write_ASCII(Write_ASCII),
    .END(out_2));
  TTY #(.rows(32), .cols(60)) tty_1 (.data(ASCII), .clk(CLK), .we(Write_ASCII), .clr(CLR));
endmodule

module Perfectos_n___ASM (
  input  in_1,
  input  in_2,
  input  in_3,
  input  [31:0] in_4,
  output out_5,
  output out_6,
  output [23:0] out_7,
  output [31:0] out_8
);

  wire c, perfectos_n_control_unit_1_li, perfectos_n_control_unit_1_lm, perfectos_n_control_unit_1_out_8,
       perfectos_n_control_unit_1_out_10, perfectos_n_control_unit_1_out_11;

  Perfectos_n____Control_Unit perfectos_n_control_unit_1 (
    .in_1(out_8), .in_2(c), .in_3(in_1), .in_4(in_2), .in_5(in_3), .write(out_5),
    .out_8(perfectos_n_control_unit_1_out_8), .LI(perfectos_n_control_unit_1_li),
    .out_10(perfectos_n_control_unit_1_out_10), .out_11(perfectos_n_control_unit_1_out_11),
    .LM(perfectos_n_control_unit_1_lm), .\end (out_6));
  Perfectos_n___Data_Path perfectos_n_data_path_1 (
    .in_1(in_4), .in_2(perfectos_n_control_unit_1_out_8), .in_3(perfectos_n_control_unit_1_lm),
    .in_4(perfectos_n_control_unit_1_out_11), .in_5(perfectos_n_control_unit_1_li),
    .in_6(perfectos_n_control_unit_1_out_10), .in_7(in_2), .in_8(in_3), .I____N(c), .out_11(out_8),
    .out_10(out_7));

  // Other names for the same wires on the sheet: clk = in_3; n[31:0] = in_4; rst = in_2; start = in_1

  // Notes on the sheet:
  //   ASM - Perfectos(n)
endmodule

module Perfectos_n____Control_Unit (
  input  [31:0] in_1,
  input  in_2,
  input  in_3,
  input  in_4,
  input  in_5,
  output \end ,
  output write,
  output out_8,
  output LI,
  output out_10,
  output out_11,
  output LM
);

  wire demultiplexer_1_out0, demultiplexer_2_out0, demultiplexer_2_out1, demultiplexer_3_out0,
       demultiplexer_3_out1, demultiplexer_4_out0, demultiplexer_4_out1, demultiplexer_5_out0, end_P, Es_P,
       IDLE_q, or_1_out, or_3_out, or_6_out, or_7_out, or_8_out, rst_P, WAIT_q, WHILE_q;

  or or_1 (or_1_out, demultiplexer_3_out1, demultiplexer_1_out0);
  or or_2 (rst_P, in_4, out_10);
  Demultiplexer #(.disabled(0), .enable("false")) demultiplexer_1 (
    .out0(demultiplexer_1_out0), .out1(out_8), .in(IDLE_q), .sel(in_3));
  D_Flip_Flop IDLE (.clk(in_5), .D(or_1_out), .Q(IDLE_q), .preset(in_4));  // open: Qn, en, reset
  or or_3 (or_3_out, out_8, out_10);
  or or_4 (LI, out_8, out_10);
  or or_5 (LM, out_8, out_11);
  Demultiplexer #(.disabled(0), .enable("false")) demultiplexer_2 (
    .out0(demultiplexer_2_out0), .out1(demultiplexer_2_out1), .in(WHILE_q), .sel(in_2));
  D_Flip_Flop WHILE (.clk(in_5), .D(or_3_out), .Q(WHILE_q), .reset(in_4));  // open: Qn, preset, en
  D_Flip_Flop AFTER_IF (.clk(in_5), .D(or_8_out), .Q(out_10), .reset(in_4));  // open: Qn, preset, en
  or or_6 (or_6_out, demultiplexer_3_out0, demultiplexer_2_out0);
  D_Flip_Flop u_END (.clk(in_5), .D(or_6_out), .Q(\end ), .reset(in_4));  // open: Qn, preset, en
  or or_7 (or_7_out, demultiplexer_4_out0, demultiplexer_2_out1);
  Demultiplexer #(.disabled(0), .enable("false")) demultiplexer_3 (
    .out0(demultiplexer_3_out0), .out1(demultiplexer_3_out1), .in(\end ), .sel(in_4));
  Demultiplexer #(.disabled(0), .enable("false")) demultiplexer_4 (
    .out0(demultiplexer_4_out0), .out1(demultiplexer_4_out1), .in(WAIT_q), .sel(end_P));
  D_Flip_Flop WAIT (.clk(in_5), .D(or_7_out), .Q(WAIT_q), .reset(in_4));  // open: Qn, preset, en
  EsPerfecto_n____ASM esperfecto_n_asm_1 (
    .in_1(in_1), .in_2(demultiplexer_2_out1), .in_3(rst_P), .in_4(in_5), .out_6(Es_P), .out_5(end_P));
  Demultiplexer #(.disabled(0), .enable("false")) demultiplexer_5 (
    .out0(demultiplexer_5_out0), .out1(out_11), .in(demultiplexer_4_out1), .sel(Es_P));
  or or_8 (or_8_out, demultiplexer_5_out0, out_11);

  assign write = out_11;

  // Other names for the same wires on the sheet: clk = in_5; I[31:0] = in_1; I____N = in_2; LI0 = out_8; LM0 = out_8;
  //   LN = out_8; rst = in_4; LI1 = out_10; rst_P0 = out_10; SI = out_10; LM1 = out_11; SM = out_11; start = in_3

  // Notes on the sheet:
  //   Status Signals
  //   Control Unit - Perfectos(n)
  //   Control Signals
endmodule

module Perfectos_n___Data_Path (
  input  [31:0] in_1,
  input  in_2,
  input  in_3,
  input  in_4,
  input  in_5,
  input  in_6,
  input  in_7,
  input  in_8,
  output I____N,
  output [23:0] out_10,
  output [31:0] out_11
);

  wire comparator_1_gt;
  wire [23:0] M___1, multiplexer_2_out;
  wire [31:0] I___1, multiplexer_1_out, N;

  Register #(.width(32)) R1 (.D(in_1), .en(in_2), .Q(N), .clk(in_8), .clr(in_7));
  Multiplexer #(.width(32), .disabled(0), .enable("false")) multiplexer_1 (
    .in0(32'h1), .in1(I___1), .out(multiplexer_1_out), .sel(in_6));
  Multiplexer #(.width(24), .disabled(0), .enable("false")) multiplexer_2 (
    .in0({24{1'b0}}), .in1(M___1), .out(multiplexer_2_out), .sel(in_4));
  Register #(.width(32)) R3 (.D(multiplexer_1_out), .en(in_5), .Q(out_11), .clk(in_8), .clr(in_7));
  Register #(.width(24)) R2 (.D(multiplexer_2_out), .en(in_3), .Q(out_10), .clk(in_8), .clr(in_7));
  not not_1 (I____N, comparator_1_gt);
  Comparator #(.width(32), .mode("unsigned")) comparator_1 (.a(out_11), .b(N), .gt(comparator_1_gt));  // open: eq, lt
  Adder #(.width(32)) adder_1 (.a(out_11), .b(32'h1), .out(I___1));  // open: cin, cout
  Adder #(.width(24)) adder_2 (.a(out_10), .b(24'h1), .out(M___1));  // open: cin, cout

  // Other names for the same wires on the sheet: clk = in_8; I[31:0] = out_11; LI = in_5; LM = in_3; LN = in_2;
  //   M[23:0] = out_10; n_t[31:0] = in_1; rst = in_7; SI = in_6; SM = in_4

  // Notes on the sheet:
  //   CONTROL SIGNALS
  //   DATA PATH - Perfectos(n)
  //   RF
  //   ALU
endmodule

module EsPerfecto_n____ASM (
  input  [31:0] in_1,
  input  in_2,
  input  in_3,
  input  in_4,
  output out_5,
  output out_6
);

  wire c1, c2, esperfecto_n_control_unit_1_lj, esperfecto_n_control_unit_1_ls,
       esperfecto_n_control_unit_1_out_7, esperfecto_n_control_unit_1_out_9,
       esperfecto_n_control_unit_1_out_10;

  EsPerfecto_n____Control_Unit esperfecto_n_control_unit_1 (
    .Status_Signals(c2), .in_2(c1), .in_3(in_2), .in_4(in_3), .in_5(in_4),
    .out_7(esperfecto_n_control_unit_1_out_7), .LS(esperfecto_n_control_unit_1_ls),
    .out_9(esperfecto_n_control_unit_1_out_9), .out_10(esperfecto_n_control_unit_1_out_10),
    .LJ(esperfecto_n_control_unit_1_lj), .\end (out_5));
  EsPerfecto_n____Data_Path esperfecto_n_data_path_1 (
    .in_1(in_1), .in_2(esperfecto_n_control_unit_1_out_7), .in_3(esperfecto_n_control_unit_1_lj),
    .in_4(esperfecto_n_control_unit_1_out_10), .in_5(esperfecto_n_control_unit_1_ls),
    .in_6(esperfecto_n_control_unit_1_out_9), .in_7(in_3), .in_8(in_4), .J___A(c1), .S___A(out_6),
    .J___A_2(c2));

  // Other names for the same wires on the sheet: clk = in_4; n[31:0] = in_1; rst = in_3; start = in_2

  // Notes on the sheet:
  //   INPUT
  //   ASM - EsPerfecto(n)
endmodule

module EsPerfecto_n____Control_Unit (
  input  Status_Signals,
  input  in_2,
  input  in_3,
  input  in_4,
  input  in_5,
  output \end ,
  output out_7,
  output LS,
  output out_9,
  output out_10,
  output LJ
);

  wire demultiplexer_1_out0, demultiplexer_2_out0, demultiplexer_2_out1, demultiplexer_3_out0,
       demultiplexer_4_out0, demultiplexer_4_out1, IDLE_q, or_1_out, or_4_out, or_5_out, or_6_out, WHILE_q;

  or or_1 (or_1_out, demultiplexer_4_out1, demultiplexer_1_out0);
  D_Flip_Flop IDLE (.clk(in_5), .D(or_1_out), .Q(IDLE_q), .preset(in_4));  // open: Qn, en, reset
  Demultiplexer #(.disabled(0), .enable("false")) demultiplexer_1 (
    .out0(demultiplexer_1_out0), .out1(out_7), .in(IDLE_q), .sel(in_3));
  or or_2 (LS, out_7, out_9);
  or or_3 (LJ, out_7, out_10);
  D_Flip_Flop WHILE (.clk(in_5), .D(or_4_out), .Q(WHILE_q), .reset(in_4));  // open: Qn, preset, en
  or or_4 (or_4_out, out_7, out_10);
  Demultiplexer #(.disabled(0), .enable("false")) demultiplexer_2 (
    .out0(demultiplexer_2_out0), .out1(demultiplexer_2_out1), .in(WHILE_q), .sel(Status_Signals));
  D_Flip_Flop AFTER_IF (.clk(in_5), .D(or_6_out), .Q(out_10), .reset(in_4));  // open: Qn, preset, en
  or or_5 (or_5_out, demultiplexer_4_out0, demultiplexer_2_out0);
  Demultiplexer #(.disabled(0), .enable("false")) demultiplexer_3 (
    .out0(demultiplexer_3_out0), .out1(out_9), .in(demultiplexer_2_out1), .sel(in_2));
  or or_6 (or_6_out, demultiplexer_3_out0, out_9);
  D_Flip_Flop u_END (.clk(in_5), .D(or_5_out), .Q(\end ), .reset(in_4));  // open: Qn, preset, en
  Demultiplexer #(.disabled(0), .enable("false")) demultiplexer_4 (
    .out0(demultiplexer_4_out0), .out1(demultiplexer_4_out1), .in(\end ), .sel(in_4));

  // Other names for the same wires on the sheet: clk = in_5; J___A = Status_Signals; J___A_t = in_2; LA = out_7;
  //   LJ_0 = out_7; LS0 = out_7; rst = in_4; LJ_1 = out_10; SJ = out_10; LS1 = out_9; SS = out_9; start = in_3

  // Notes on the sheet:
  //   CONTROL UNIT - EsPerfecto(n)
  //   Control Signals
endmodule

module EsPerfecto_n____Data_Path (
  input  [31:0] in_1,
  input  in_2,
  input  in_3,
  input  in_4,
  input  in_5,
  input  in_6,
  input  in_7,
  input  in_8,
  output J___A_2,
  output J___A,
  output S___A
);

  wire comparator_1_gt;
  wire [31:0] A, A_2, A___J, J, J___1, multiplexer_1_out, multiplexer_2_out, S, S___J;

  Multiplexer #(.width(32), .disabled(0), .enable("false")) multiplexer_1 (
    .in0(32'h1), .in1(J___1), .out(multiplexer_1_out), .sel(in_4));
  Multiplexer #(.width(32), .disabled(0), .enable("false")) multiplexer_2 (
    .in0({32{1'b0}}), .in1(S___J), .out(multiplexer_2_out), .sel(in_6));
  Register #(.width(32)) R1 (.D(in_1), .en(in_2), .Q(A), .clk(in_8), .clr(in_7));
  Register #(.width(32)) R2 (.D(multiplexer_1_out), .en(in_3), .Q(J), .clk(in_8), .clr(in_7));
  Register #(.width(32)) R3 (.D(multiplexer_2_out), .en(in_5), .Q(S), .clk(in_8), .clr(in_7));
  Adder #(.width(32)) adder_1 (.a(J), .b(32'h1), .out(J___1));  // open: cin, cout
  Adder #(.width(32)) adder_2 (.a(J), .b(S), .out(S___J));  // open: cin, cout
  Divider #(.width(32)) divider_1 (.a(A), .b(32'h2), .out(A_2));  // open: upper, rem
  Divider #(.width(32)) divider_2 (.a(A), .b(J), .rem(A___J));  // open: out, upper
  Comparator #(.width(32), .mode("unsigned")) comparator_1 (.a(J), .b(A_2), .gt(comparator_1_gt));  // open: eq, lt
  Comparator #(.width(32), .mode("unsigned")) comparator_2 (.a(A___J), .b({32{1'b0}}), .eq(J___A));  // open: gt, lt
  Comparator #(.width(32), .mode("unsigned")) comparator_3 (.a(S), .b(A), .eq(S___A));  // open: gt, lt
  not not_1 (J___A_2, comparator_1_gt);

  // Other names for the same wires on the sheet: clk = in_8; LA = in_2; LJ = in_3; LS = in_5; n[31:0] = in_1;
  //   rst = in_7; SJ = in_4; SS = in_6

  // Notes on the sheet:
  //   CONTROL SIGNALS
  //   Data Path - EsPerfecto(n)
  //   RF
  //   ALU
endmodule

module starter (
  input  in_1,
  input  in_2,
  output start
);

  wire en, not_1_out;

  not not_1 (not_1_out, in_1);
  D_Flip_Flop d_ff_1 (.clk(in_2), .D(1'b1), .Qn(en), .en(not_1_out), .reset(in_1));  // open: Q, preset
  and and_1 (start, ~in_1, en);  // AND_Gate

  // Other names for the same wires on the sheet: clk = in_2; rst = in_1

  // Notes on the sheet:
  //   STARTER
endmodule

module PrintMany (
  input  [31:0] in_1,
  input  [23:0] in_2,
  input  in_3,
  input  in_4,
  input  in_5,
  output out_6,
  output [23:0] out_7,
  output out_8,
  output [6:0] out_9
);

  wire printmany_control_unit_1_li, printmany_control_unit_1_out_7, printmany_control_unit_1_out_10,
       printmany_data_path_1_i___m;

  PrintMany___Control_Unit printmany_control_unit_1 (
    .Status_Signals(printmany_data_path_1_i___m), .in_2(in_3), .in_3(in_4), .in_5(in_1),
    .out_7(printmany_control_unit_1_out_7), .w(out_8), .LI(printmany_control_unit_1_li),
    .out_10(printmany_control_unit_1_out_10), .ASCII(out_9), .\end (out_6), .in_4(in_5));
  PrintMany___Data_Path printmany_data_path_1 (
    .in_1(in_2), .in_2(printmany_control_unit_1_out_7), .in_3(printmany_control_unit_1_li),
    .in_4(printmany_control_unit_1_out_10), .in_5(in_5), .in_6(in_4), .out_7(out_7),
    .I___M(printmany_data_path_1_i___m));

  // Other names for the same wires on the sheet: clk = in_5; rst = in_4; start = in_3
endmodule

module PrintMany___Data_Path (
  input  [23:0] in_1,
  input  in_2,
  input  in_3,
  input  in_4,
  input  in_5,
  input  in_6,
  output [23:0] out_7,
  output I___M
);

  wire [23:0] I___1, M, multiplexer_1_out;

  Register #(.width(24)) R1 (.D(in_1), .en(in_2), .Q(M), .clk(in_5), .clr(in_6));
  Multiplexer #(.width(24), .disabled(0), .enable("false")) multiplexer_1 (
    .in0({24{1'b0}}), .in1(I___1), .out(multiplexer_1_out), .sel(in_4));
  Register #(.width(24)) R2 (.D(multiplexer_1_out), .en(in_3), .Q(out_7), .clk(in_5), .clr(in_6));
  Adder #(.width(24)) adder_1 (.a(out_7), .b(24'h1), .out(I___1));  // open: cin, cout
  Comparator #(.width(24), .mode("unsigned")) comparator_1 (.a(out_7), .b(M), .lt(I___M));  // open: gt, eq

  // Other names for the same wires on the sheet: clk = in_5; I[23:0] = out_7; LI = in_3; LM = in_2; m_t[23:0] = in_1;
  //   rst = in_6; SI = in_4

  // Notes on the sheet:
  //   Control Signals
  //   Data Path - PrintMany(m)
  //   RF
  //   ALU
endmodule

module PrintMany___Control_Unit (
  input  Status_Signals,
  input  in_2,
  input  in_3,
  input  in_4,
  input  [31:0] in_5,
  output \end ,
  output out_7,
  output w,
  output LI,
  output out_10,
  output [6:0] ASCII
);

  wire demultiplexer_1_out0, demultiplexer_2_out0, demultiplexer_2_out1, demultiplexer_3_out0,
       demultiplexer_3_out1, demultiplexer_4_out0, end_P, IDLE_q, or_1_out, or_2_out, or_3_out, or_4_out, w0,
       WAIT_q, WHILE_q;
  wire [6:0] ASCII0;

  or or_1 (or_1_out, demultiplexer_3_out1, demultiplexer_1_out0);
  D_Flip_Flop IDLE (.clk(in_4), .D(or_1_out), .Q(IDLE_q), .preset(in_3));  // open: Qn, en, reset
  Demultiplexer #(.disabled(0), .enable("false")) demultiplexer_1 (
    .out0(demultiplexer_1_out0), .out1(out_7), .in(IDLE_q), .sel(in_2));
  or or_2 (or_2_out, out_7, out_10);
  D_Flip_Flop WHILE (.clk(in_4), .D(or_2_out), .Q(WHILE_q), .reset(in_3));  // open: Qn, preset, en
  Demultiplexer #(.disabled(0), .enable("false")) demultiplexer_2 (
    .out0(demultiplexer_2_out0), .out1(demultiplexer_2_out1), .in(WHILE_q), .sel(Status_Signals));
  or or_3 (or_3_out, demultiplexer_3_out0, demultiplexer_2_out0);
  D_Flip_Flop u_END (.clk(in_4), .D(or_3_out), .Q(\end ), .reset(in_3));  // open: Qn, preset, en
  or or_4 (or_4_out, demultiplexer_4_out0, demultiplexer_2_out1);
  Demultiplexer #(.disabled(0), .enable("false")) demultiplexer_3 (
    .out0(demultiplexer_3_out0), .out1(demultiplexer_3_out1), .in(\end ), .sel(in_3));
  Demultiplexer #(.disabled(0), .enable("false")) demultiplexer_4 (
    .out0(demultiplexer_4_out0), .out1(out_10), .in(WAIT_q), .sel(end_P));
  D_Flip_Flop WAIT (.clk(in_4), .D(or_4_out), .Q(WAIT_q), .reset(in_3));  // open: Qn, preset, en
  PRINT_UDEC print_udec_1 (
    .num(in_5), .start(demultiplexer_2_out1), .CLK(in_4), .RST(in_3), .ASCII(ASCII0), .Write_ASCII(w0),
    .\end (end_P));
  or or_5 (LI, out_7, out_10);
  or or_6 (w, w0, out_10);
  Multiplexer #(.width(7), .disabled(0), .enable("false")) multiplexer_1 (
    .in0(ASCII0), .in1(7'b0100000), .out(ASCII), .sel(out_10));

  // Other names for the same wires on the sheet: CLK = in_4; I___M = Status_Signals; LI0 = out_7; LM = out_7;
  //   M_I[31:0] = in_5; rst = in_3; start = in_2; LI1 = out_10; SI = out_10; w1 = out_10

  // Notes on the sheet:
  //   Control Unit - PrintMany
endmodule

module PrintMany___starter (
  input  in_1,
  input  in_2,
  input  in_3,
  output start
);

  wire en;

  D_Flip_Flop d_ff_1 (.clk(in_2), .D(1'b1), .Qn(en), .en(in_1), .reset(in_3));  // open: Q, preset
  and and_1 (start, in_1, en);

  // Other names for the same wires on the sheet: clk = in_2; end = in_1; rst = in_3
endmodule
