// Logisim project Min.circ as structural Verilog
module BOARD_BIG_ASM (
  output out_1
);

  wire button_1_out, CLK, CLR, d_ff_1_q, not_1_out, Write, Write_ASCII;
  wire [6:0] ASCII;
  wire [7:0] counter_1_q;
  wire [23:0] Dir_INPUT, Dir_MEMORY;
  wire [31:0] INPUT, MEMORY_IN, MEMORY_OUT;

  Button button_1 (.out(button_1_out));
  Clock clock_1 (.out(CLK));
  D_Flip_Flop d_ff_1 (.clk(CLK), .D(1'b1), .Q(d_ff_1_q), .reset(button_1_out));  // open: Qn, preset, en
  D_Flip_Flop d_ff_2 (.clk(CLK), .D(d_ff_1_q), .Qn(CLR), .reset(button_1_out));  // open: Q, preset, en
  BIG_ASM big_asm_1 (
    .DATA_INPUT(INPUT), .MEMORY_IN(MEMORY_OUT), .CLK(CLK), .CLR(CLR), .DIR_INPUT(Dir_INPUT),
    .MEMORY_OUT(MEMORY_IN), .DIR_MEMORY(Dir_MEMORY), .Write_OUTPUT(Write), .ASCII(ASCII),
    .Write_ASCII(Write_ASCII), .END(out_1));
  MEMORY memory_1 (.DIR(Dir_MEMORY), .DATA_IN(MEMORY_IN), .WRITE(Write), .CLK(CLK), .CLR(CLR), .DATA_OUT(MEMORY_OUT));
  INPUT input_1 (.DIR(Dir_INPUT), .CLK(CLK), .DATA_OUT(INPUT));
  Counter counter_1 (.load(1'b0), .count(not_1_out), .Q(counter_1_q), .clk(CLK), .clr(CLR));  // open: D, carry
  not not_1 (not_1_out, out_1);
  // Probe on counter_1_q
  TTY #(.rows(32), .cols(60)) tty_1 (.data(ASCII), .clk(CLK), .we(Write_ASCII), .clr(CLR));

  // Other names for the same wires on the sheet: END = out_1

  // Notes on the sheet:
  //   COUNTER
  //   BOARD
endmodule

module INPUT (
  input  [23:0] DIR,
  input  CLK,
  output [31:0] DATA_OUT
);

  RAM #(.addrWidth(24), .dataWidth(32)) ram_1 (.addr(DIR), .data(DATA_OUT), .clk(CLK), .ld(1'b1));  // open: sel, clr
endmodule

module MEMORY (
  input  [23:0] DIR,
  input  [31:0] DATA_IN,
  input  WRITE,
  input  CLK,
  input  CLR,
  output [31:0] DATA_OUT
);

  wire not_1_out;

  not not_1 (not_1_out, WRITE);
  RAM #(.addrWidth(24), .dataWidth(32), .bus("separate")) ram_1 (
    .addr(DIR), .din(DATA_IN), .data(DATA_OUT), .clk(CLK), .ld(not_1_out), .clr(CLR));  // open: str, sel
endmodule

module BIG_ASM (
  input  [31:0] DATA_INPUT,
  input  [31:0] MEMORY_IN,
  input  CLK,
  input  CLR,
  output [23:0] DIR_INPUT,
  output [31:0] MEMORY_OUT,
  output [23:0] DIR_MEMORY,
  output Write_OUTPUT,
  output [6:0] ASCII,
  output Write_ASCII,
  output END
);

  wire control_unit_1_lb, control_unit_1_lmin, control_unit_1_out_9, control_unit_1_out_11,
       data_path_1_a_b____min, data_path_1_b___c, start;
  wire [1:0] control_unit_1_index_sel;
  wire [31:0] min;

  starter starter_1 (.in_1(CLR), .in_2(CLK), .start(start));
  Control_Unit control_unit_1 (
    .in_1(data_path_1_b___c), .in_2(data_path_1_a_b____min), .in_3(CLK), .in_4(start), .in_5(CLR),
    .INDEX_SEL(control_unit_1_index_sel), .LB(control_unit_1_lb), .LMin(control_unit_1_lmin),
    .out_11(control_unit_1_out_11), .END(END), .out_9(control_unit_1_out_9));
  PRINT_DEC print_dec_1 (
    .num(min), .start(END), .CLK(CLK), .RST(CLR), .ASCII(ASCII), .Write_ASCII(Write_ASCII));  // open: END
  Data_Path data_path_1 (
    .in_1(DATA_INPUT), .in_2(control_unit_1_lb), .in_4(control_unit_1_out_11), .in_6(control_unit_1_lmin),
    .in_3(control_unit_1_out_9), .in_5(CLK), .in_7(CLR), .B___C(data_path_1_b___c),
    .A_B____MIN(data_path_1_a_b____min), .ind(DIR_INPUT), .S_Ind(control_unit_1_index_sel), .out_12(min));

  assign Write_OUTPUT = 1'b0;

  // Other names for the same wires on the sheet: rst = CLR
endmodule

module PRINT_UDEC (
  input  [31:0] num,
  input  start,
  input  CLK,
  input  RST,
  output [6:0] ASCII,
  output Write_ASCII,
  output \end 
);

  wire _0_c, _0_n, demultiplexer_1_out0, demultiplexer_2_out0, demultiplexer_2_out1, demultiplexer_3_out0,
       demultiplexer_3_out1, IDLE_2_q, IDLE_3_q, IDLE_4_q, IDLE_q, Lc, Lc_0, Ln, Ln_0, or_1_out;
  wire [23:0] bit_extender_1_out;
  wire [31:0] c, c___1, c___1_t, divider_1_rem, memory_1_data_out, multiplexer_1_out, multiplexer_2_out,
       multiplexer_3_out, n, n___10, n___10___48;

  Multiplexer #(.width(32), .enable("false")) multiplexer_1 (
    .in0(num), .in1(n___10), .out(multiplexer_1_out), .sel(Lc_0));
  Divider #(.width(32)) divider_1 (.a(n), .b(32'ha), .out(n___10), .rem(divider_1_rem));  // open: upper
  Adder #(.width(32)) adder_1 (.a(divider_1_rem), .b(32'h30), .out(n___10___48));  // open: cin, cout
  or or_1 (or_1_out, demultiplexer_1_out0, \end );
  Register #(.width(32)) u_n (.D(multiplexer_1_out), .en(Ln), .Q(n), .clk(CLK), .clr(RST));
  D_Flip_Flop IDLE (.clk(CLK), .D(or_1_out), .Q(IDLE_q), .preset(RST));  // open: Qn, en, reset
  Demultiplexer #(.enable("false")) demultiplexer_1 (
    .out0(demultiplexer_1_out0), .out1(Ln_0), .in(IDLE_q), .sel(start));
  or or_2 (Write_ASCII, demultiplexer_3_out0, demultiplexer_2_out1);
  Multiplexer #(.width(32), .enable("false")) multiplexer_2 (
    .in0(c___1), .in1(c___1_t), .out(multiplexer_2_out), .sel(Write_ASCII));
  Adder #(.width(32)) adder_2 (.a(c), .b(32'h1), .out(c___1));  // open: cin, cout
  Subtractor #(.width(32)) subtractor_1 (.a(c), .b(32'h1), .out(c___1_t));  // open: bin, bout
  D_Flip_Flop IDLE_2 (.clk(CLK), .D(Ln_0), .Q(IDLE_2_q), .reset(RST));  // open: Qn, preset, en
  Register #(.width(32)) u_c (.D(multiplexer_2_out), .en(Lc), .Q(c), .clk(CLK), .clr(RST));
  or or_3 (Lc_0, IDLE_2_q, demultiplexer_3_out1);
  Multiplexer #(.width(32), .enable("false")) multiplexer_3 (
    .in0(c), .in1(c___1_t), .out(multiplexer_3_out), .sel(Write_ASCII));
  Comparator #(.width(32), .mode("unsigned")) comparator_1 (.a({32{1'b0}}), .b(n), .lt(_0_n));  // open: gt, eq
  Comparator #(.width(32), .mode("unsigned")) comparator_2 (.a({32{1'b0}}), .b(c), .lt(_0_c));  // open: gt, eq
  D_Flip_Flop IDLE_3 (.clk(CLK), .D(Write_ASCII), .Q(IDLE_3_q), .reset(RST));  // open: Qn, preset, en
  Demultiplexer #(.enable("false")) demultiplexer_2 (
    .out0(demultiplexer_2_out0), .out1(demultiplexer_2_out1), .in(IDLE_3_q), .sel(_0_c));
  Bit_Extender #(.in_width(32), .out_width(24)) bit_extender_1 (.in(multiplexer_3_out), .out(bit_extender_1_out));
  D_Flip_Flop IDLE_4 (.clk(CLK), .D(Lc_0), .Q(IDLE_4_q), .reset(RST));  // open: Qn, preset, en
  or or_4 (Lc, Lc_0, Write_ASCII);
  or or_5 (Ln, Ln_0, Lc_0);
  Demultiplexer #(.enable("false")) demultiplexer_3 (
    .out0(demultiplexer_3_out0), .out1(demultiplexer_3_out1), .in(IDLE_4_q), .sel(_0_n));
  D_Flip_Flop IDLE_5 (.clk(CLK), .D(demultiplexer_2_out0), .Q(\end ), .reset(RST));  // open: Qn, preset, en
  MEMORY memory_1 (
    .DIR(bit_extender_1_out), .DATA_IN(n___10___48), .WRITE(Lc_0), .CLK(CLK), .CLR(RST),
    .DATA_OUT(memory_1_data_out));
  Bit_Extender #(.in_width(32), .out_width(7)) bit_extender_2 (.in(memory_1_data_out), .out(ASCII));

  // Other names for the same wires on the sheet: Lc_1 = Write_ASCII; Sc = Write_ASCII; Ln_1 = Lc_0; Sn = Lc_0;
  //   Write = Lc_0
endmodule

module PRINT_DEC (
  input  [31:0] num,
  input  start,
  input  CLK,
  input  RST,
  output [6:0] ASCII,
  output Write_ASCII,
  output END
);

  wire d_ff_1_q, demultiplexer_1_out0, demultiplexer_1_out1, demultiplexer_2_out0, demultiplexer_3_out0,
       demultiplexer_4_out0, demultiplexer_4_out1, end_t, IDLE_3_q, IDLE_q, or_1_out, or_2_out, or_3_out,
       or_5_out, S_ASCII, startUDEC, Write_ASCII_1;
  wire [6:0] ASCII_t;
  wire [31:0] multiplexer_1_out, negator_1_out;

  or or_1 (or_1_out, demultiplexer_1_out0, demultiplexer_4_out1);
  Negator #(.width(32)) negator_1 (.in(num), .out(negator_1_out));
  D_Flip_Flop IDLE (.clk(CLK), .D(or_1_out), .Q(IDLE_q), .preset(RST));  // open: Qn, en, reset
  Demultiplexer #(.enable("false")) demultiplexer_1 (
    .out0(demultiplexer_1_out0), .out1(demultiplexer_1_out1), .in(IDLE_q), .sel(start));
  Multiplexer #(.width(32), .enable("false")) multiplexer_1 (
    .in0(num), .in1(negator_1_out), .out(multiplexer_1_out), .sel(num[31]));
  Demultiplexer #(.enable("false")) demultiplexer_2 (
    .out0(demultiplexer_2_out0), .out1(S_ASCII), .in(demultiplexer_1_out1), .sel(num[31]));
  or or_2 (or_2_out, demultiplexer_2_out0, S_ASCII);
  D_Flip_Flop IDLE_2 (.clk(CLK), .D(or_2_out), .Q(startUDEC), .reset(RST));  // open: Qn, preset, en
  PRINT_UDEC print_udec_1 (
    .num(multiplexer_1_out), .start(startUDEC), .CLK(CLK), .RST(RST), .ASCII(ASCII_t),
    .Write_ASCII(Write_ASCII_1), .\end (end_t));
  D_Flip_Flop IDLE_3 (.clk(CLK), .D(or_3_out), .Q(IDLE_3_q), .reset(RST));  // open: Qn, preset, en
  or or_3 (or_3_out, startUDEC, demultiplexer_3_out0);
  Demultiplexer #(.enable("false")) demultiplexer_3 (
    .out0(demultiplexer_3_out0), .out1(END), .in(IDLE_3_q), .sel(end_t));
  Multiplexer #(.width(7), .enable("false")) multiplexer_2 (
    .in0(ASCII_t), .in1(7'b0101101), .out(ASCII), .sel(S_ASCII));
  or or_4 (Write_ASCII, S_ASCII, Write_ASCII_1);
  or or_5 (or_5_out, END, demultiplexer_4_out0);
  D_Flip_Flop d_ff_1 (.clk(CLK), .D(or_5_out), .Q(d_ff_1_q));  // open: Qn, preset, en, reset
  Demultiplexer #(.enable("false")) demultiplexer_4 (
    .out0(demultiplexer_4_out0), .out1(demultiplexer_4_out1), .in(d_ff_1_q), .sel(RST));

  // Other names for the same wires on the sheet: sign = num[31]; Write_ASCII_0 = S_ASCII
endmodule

module TEST_PRINT (
  input  [31:0] in_1,
  output out_2
);

  wire button_1_out, button_2_out, CLK, CLR, d_ff_1_q, Write_ASCII;
  wire [6:0] ASCII;

  Button button_1 (.out(button_1_out));
  Clock clock_1 (.out(CLK));
  D_Flip_Flop d_ff_1 (.clk(CLK), .D(1'b1), .Q(d_ff_1_q), .reset(button_1_out));  // open: Qn, preset, en
  D_Flip_Flop d_ff_2 (.clk(CLK), .D(d_ff_1_q), .Qn(CLR), .reset(button_1_out));  // open: Q, preset, en
  Button button_2 (.out(button_2_out));
  PRINT_UDEC print_udec_1 ();  // open: num, start, CLK, RST, ASCII, Write_ASCII, end
  PRINT_DEC print_dec_1 (
    .num(in_1), .start(button_2_out), .CLK(CLK), .RST(CLR), .ASCII(ASCII), .Write_ASCII(Write_ASCII),
    .END(out_2));
  TTY #(.rows(32), .cols(60)) tty_1 (.data(ASCII), .clk(CLK), .we(Write_ASCII), .clr(CLR));
endmodule

module Data_Path (
  input  [31:0] in_1,
  input  in_2,
  input  in_3,
  input  in_4,
  input  in_5,
  input  in_6,
  input  in_7,
  input  [1:0] S_Ind,
  output B___C,
  output A_B____MIN,
  output [23:0] ind,
  output [31:0] out_12
);

  wire [23:0] bit_extender_1_out, bit_extender_2_out, DIR_A_B, DIR_A_C;
  wire [31:0] B, B___1, C, multiplexer_2_out;

  Multiplexer #(.select(2), .width(24), .disabled(0), .enable("false")) multiplexer_1 (
    .in0({24{1'b0}}), .in1(24'h1), .in2(DIR_A_C), .in3(DIR_A_B), .out(ind), .sel(S_Ind));
  Register #(.width(32)) r1 (.D(in_1), .en(in_6), .Q(out_12), .clk(in_5), .clr(in_7));
  Register #(.width(32)) r2 (.D(in_1), .en(in_4), .Q(C), .clk(in_5), .clr(in_7));
  Multiplexer #(.width(32), .disabled(0), .enable("false")) multiplexer_2 (
    .in0(in_1), .in1(B___1), .out(multiplexer_2_out), .sel(in_3));
  Register #(.width(32)) r3 (.D(multiplexer_2_out), .en(in_2), .Q(B), .clk(in_5), .clr(in_7));
  Comparator #(.width(32), .mode("unsigned")) comparator_1 (.a(B), .b(C), .lt(B___C));  // open: gt, eq
  Bit_Extender #(.in_width(32), .out_width(24)) bit_extender_1 (.in(B), .out(bit_extender_1_out));
  Bit_Extender #(.in_width(32), .out_width(24)) bit_extender_2 (.in(C), .out(bit_extender_2_out));
  Adder #(.width(32)) adder_1 (.a(B), .b(32'h1), .out(B___1));  // open: cin, cout
  Adder #(.width(24)) adder_2 (.a(bit_extender_1_out), .b(24'h3), .out(DIR_A_B));  // open: cin, cout
  Adder #(.width(24)) adder_3 (.a(bit_extender_2_out), .b(24'h3), .out(DIR_A_C));  // open: cin, cout
  Comparator #(.width(32), .mode("unsigned")) comparator_2 (.a(in_1), .b(out_12), .lt(A_B____MIN));  // open: gt, eq

  // Other names for the same wires on the sheet: clk = in_5; LB = in_2; LC = in_4; LMin = in_6; M_ind[31:0] = in_1;
  //   MIN[31:0] = out_12; rst = in_7; SB = in_3

  // Notes on the sheet:
  //   Dir B
  //   Dir C
  //   CONTROL SIGNALS
  //   INDEX
  //   OUTPUT
  //   DATA PATH
  //   (para acceder a los datos de entrada)
  //   REGISTER FILE
  //   ALU
endmodule

module Control_Unit (
  input  in_1,
  input  in_2,
  input  in_3,
  input  in_4,
  input  in_5,
  output END,
  output [1:0] INDEX_SEL,
  output LB,
  output out_9,
  output LMin,
  output out_11
);

  wire demultiplexer_1_out0, demultiplexer_2_out0, demultiplexer_2_out1, demultiplexer_3_out0,
       demultiplexer_4_out0, demultiplexer_4_out1, I01, I10, IDLE_q, LB0, LMin1, or_1_out, or_6_out,
       or_7_out, or_8_out;

  or or_1 (or_1_out, demultiplexer_4_out1, demultiplexer_1_out0);
  D_Flip_Flop IDLE (.clk(in_3), .D(or_1_out), .Q(IDLE_q), .preset(in_5));  // open: Qn, en, reset
  Demultiplexer #(.enable("false")) demultiplexer_1 (.out0(demultiplexer_1_out0), .out1(LB0), .in(IDLE_q), .sel(in_4));
  D_Flip_Flop WAIT (.clk(in_3), .D(LB0), .Q(out_11), .reset(in_5));  // open: Qn, preset, en
  or or_2 (INDEX_SEL[0], out_11, I01);
  or or_3 (INDEX_SEL[1], I10, I01);
  or or_4 (LB, LB0, out_9);
  or or_5 (LMin, I10, LMin1);
  D_Flip_Flop WAIT_2 (.clk(in_3), .D(out_11), .Q(I10), .reset(in_5));  // open: Qn, preset, en
  or or_6 (or_6_out, I10, out_9);
  D_Flip_Flop WHILE (.clk(in_3), .D(or_6_out), .Q(I01), .reset(in_5));  // open: Qn, preset, en
  or or_7 (or_7_out, demultiplexer_4_out0, demultiplexer_2_out0);
  Demultiplexer #(.enable("false")) demultiplexer_2 (
    .out0(demultiplexer_2_out0), .out1(demultiplexer_2_out1), .in(I01), .sel(in_1));
  D_Flip_Flop u_END (.clk(in_3), .D(or_7_out), .Q(END), .reset(in_5));  // open: Qn, preset, en
  Demultiplexer #(.enable("false")) demultiplexer_3 (
    .out0(demultiplexer_3_out0), .out1(LMin1), .in(demultiplexer_2_out1), .sel(in_2));
  D_Flip_Flop AFTER_IF (.clk(in_3), .D(or_8_out), .Q(out_9), .reset(in_5));  // open: Qn, preset, en
  Demultiplexer #(.enable("false")) demultiplexer_4 (
    .out0(demultiplexer_4_out0), .out1(demultiplexer_4_out1), .in(END), .sel(in_5));
  or or_8 (or_8_out, demultiplexer_3_out0, LMin1);

  // Other names for the same wires on the sheet: A_B____MIN = in_2; B___C = in_1; clk = in_3; I11 = I01; I00 = out_11;
  //   LC = out_11; LMin0 = I10; rst = in_5; LB1 = out_9; SB = out_9; start = in_4

  // Notes on the sheet:
  //   STATUS SIGNALS
  //   CONTROL SIGNALS
endmodule

module starter (
  input  in_1,
  input  in_2,
  output start
);

  wire en, not_1_out;

  not not_1 (not_1_out, in_1);
  D_Flip_Flop d_ff_1 (.clk(in_2), .D(1'b1), .Qn(en), .en(not_1_out), .reset(in_1));  // open: Q, preset
  and and_1 (start, ~in_1, en);  // AND_Gate

  // Other names for the same wires on the sheet: clk = in_2; clr = in_1

  // Notes on the sheet:
  //   STARTER
endmodule

module Printer___Starter (
  input  in_1,
  input  in_2,
  input  in_3,
  output out_4
);

  wire en;

  D_Flip_Flop d_ff_1 (.clk(in_2), .Qn(en), .en(in_1), .reset(in_3));  // open: D, Q, preset
  and and_1 (out_4, in_1, en);

  // Other names for the same wires on the sheet: clk = in_2; end = in_1; rst = in_3
endmodule
